# Fritzing sketch NodeMCU-RemoteController_schema (saved by Fritzing 0.9.3b)
circuit board: 3.08058cm x 4.81719cm
breadboards: 1

parts:
  U1 = NodeMCU V1.0
  D1 = LTE-302 [package=lte-302]
  J1 = female pin header, 2 pins [form="♀ (female)"]

nets:
  N1: U1.GND, D1.C, J1.pin1
  N2: U1.D5, D1.A, J1.pin2

custom parts:
  NodeMCU V1.0: ESP8266 based NodeMCU
